// Logisim project Lab2 (1).circ as structural Verilog: 7 circuits, main circuit main
module FF_D (
  input  in_1,
  input  in_2,
  input  in_3,
  input  in_4,
  input  in_5,
  output out_6,
  output out_7,
  output out_8,
  output out_9,
  output out_10,
  output out_11,
  output out_12,
  output out_13
);

  wire A_qn, B_qn, C_qn, D_qn;

  D_Flip_Flop A (.clk(in_1), .D(in_2), .Q(out_6), .Qn(A_qn));  // open: preset, en, reset
  D_Flip_Flop B (.clk(in_1), .D(in_3), .Q(out_7), .Qn(B_qn));  // open: preset, en, reset
  D_Flip_Flop C (.clk(in_1), .D(in_4), .Q(out_8), .Qn(C_qn));  // open: preset, en, reset
  D_Flip_Flop D (.clk(in_1), .D(in_5), .Q(out_9), .Qn(D_qn));  // open: preset, en, reset
  Da da_1 (.in_1(out_6), .in_2(out_7), .in_3(out_8), .in_4(out_9), .out_5(out_10));
  Db db_1 (.A(out_6), .B(out_7), .nB(B_qn), .nC(C_qn), .D(out_9), .out_6(out_11));
  Dc dc_1 (.A(out_6), .B(out_7), .nB(B_qn), .C(out_8), .nC(C_qn), .D(out_9), .nD(D_qn), .out_8(out_12));
  Dd dd_1 (.A(out_6), .nA(A_qn), .B(out_7), .nB(B_qn), .C(out_8), .nC(C_qn), .nD(D_qn), .out_8(out_13));
endmodule

module Da (
  input  in_1,
  input  in_2,
  input  in_3,
  input  in_4,
  output out_5
);

  wire and_1_out, and_2_out;

  and and_1 (and_1_out, in_2, in_3);
  and and_2 (and_2_out, in_2, in_4);
  or or_1 (out_5, in_1, and_1_out, and_2_out);
endmodule

module Dc (
  input  A,
  input  B,
  input  nB,
  input  C,
  input  nC,
  input  D,
  input  nD,
  output out_8
);

  wire and_1_out, and_2_out, and_3_out;

  and and_1 (and_1_out, A, B, C);
  and and_2 (and_2_out, A, nC, D);
  and and_3 (and_3_out, nB, C, nD);
  or or_1 (out_8, and_1_out, and_2_out, and_3_out);
endmodule

module Db (
  input  A,
  input  B,
  input  nB,
  input  nC,
  input  D,
  output out_6
);

  wire and_1_out, and_2_out, and_3_out;

  and and_1 (and_1_out, A, B);
  and and_2 (and_2_out, B, nC);
  and and_3 (and_3_out, nB, D);
  or or_1 (out_6, and_1_out, and_2_out, and_3_out);
endmodule

module Dd (
  input  A,
  input  nA,
  input  B,
  input  nB,
  input  C,
  input  nC,
  input  nD,
  output out_8
);

  wire and_1_out, and_2_out, and_3_out, and_4_out;

  and and_1 (and_1_out, A, B, C);
  and and_2 (and_2_out, nA, B, nC);
  and and_3 (and_3_out, nB, nD);
  and and_4 (and_4_out, nC, nD);
  or or_1 (out_8, and_1_out, and_2_out, and_3_out, and_4_out);
endmodule

module _7_sig (
  input  A,
  input  B,
  input  C,
  input  D,
  output a_2,
  output b_2,
  output c_2,
  output d_2,
  output e,
  output f,
  output g
);

  wire and_1_out, and_2_out, and_3_out, and_4_out, and_5_out, and_6_out, and_7_out, and_8_out, and_9_out,
       and_10_out, and_11_out, and_12_out, and_13_out, and_14_out, and_15_out, and_16_out, and_17_out,
       and_18_out, and_19_out, and_20_out, and_21_out, and_22_out, and_23_out, and_24_out, not_1_out,
       not_2_out, not_3_out, not_4_out, not_5_out, not_6_out, not_7_out, not_8_out, not_9_out, not_10_out,
       not_11_out, not_12_out, not_13_out, not_14_out, not_15_out, not_16_out, not_17_out, not_18_out,
       not_19_out, not_20_out, not_21_out, not_22_out, not_23_out, not_24_out, not_25_out, not_26_out,
       not_27_out, not_28_out, not_29_out, not_30_out, not_31_out, not_32_out;

  not not_1 (not_1_out, C);
  and and_1 (and_1_out, not_1_out, not_2_out);
  not not_2 (not_2_out, D);
  not not_3 (not_3_out, B);
  and and_2 (and_2_out, not_3_out, C, D);
  and and_3 (and_3_out, B, not_4_out);
  not not_4 (not_4_out, C);
  not not_5 (not_5_out, A);
  and and_4 (and_4_out, not_5_out, not_6_out, not_7_out);
  not not_6 (not_6_out, B);
  not not_7 (not_7_out, C);
  not not_8 (not_8_out, C);
  and and_5 (and_5_out, not_8_out, D);
  and and_6 (and_6_out, C, not_9_out);
  not not_9 (not_9_out, D);
  and and_7 (and_7_out, B, C);
  and and_8 (and_8_out, A, C);
  and and_9 (and_9_out, A, B);
  or or_1 (c_2, D, C, B, A);
  not not_10 (not_10_out, A);
  not not_11 (not_11_out, C);
  not not_12 (not_12_out, D);
  not not_13 (not_13_out, A);
  not not_14 (not_14_out, B);
  not not_15 (not_15_out, B);
  not not_16 (not_16_out, C);
  not not_17 (not_17_out, D);
  not not_18 (not_18_out, B);
  and and_10 (and_10_out, not_18_out, not_19_out, not_20_out);
  not not_19 (not_19_out, C);
  not not_20 (not_20_out, D);
  and and_11 (and_11_out, A, C, not_21_out);
  not not_21 (not_21_out, D);
  not not_22 (not_22_out, A);
  not not_23 (not_23_out, B);
  and and_12 (and_12_out, not_22_out, not_23_out, D);
  and and_13 (and_13_out, B, not_24_out);
  not not_24 (not_24_out, D);
  and and_14 (and_14_out, B, C);
  and and_15 (and_15_out, A, not_25_out);
  not not_25 (not_25_out, D);
  not not_26 (not_26_out, B);
  and and_16 (and_16_out, not_26_out, not_27_out);
  not not_27 (not_27_out, C);
  not not_28 (not_28_out, C);
  and and_17 (and_17_out, not_28_out, not_29_out);
  not not_29 (not_29_out, D);
  not not_30 (not_30_out, A);
  and and_18 (and_18_out, not_30_out, not_31_out, D);
  not not_31 (not_31_out, B);
  and and_19 (and_19_out, B, C);
  and and_20 (and_20_out, A, not_32_out);
  not not_32 (not_32_out, D);
  or or_2 (a_2, and_1_out, and_2_out, and_3_out, A);
  and and_21 (and_21_out, not_10_out, not_11_out, not_12_out);
  and and_22 (and_22_out, not_13_out, not_14_out, C, D);
  and and_23 (and_23_out, A, not_15_out, not_16_out);
  and and_24 (and_24_out, A, C, not_17_out);
  or or_3 (e, and_10_out, and_11_out);
  or or_4 (f, and_12_out, and_13_out, and_14_out, and_15_out);
  or or_5 (g, and_16_out, and_17_out, and_18_out, and_19_out, and_20_out);
  or or_6 (b_2, and_4_out, and_5_out, and_6_out, and_7_out, and_8_out, and_9_out);
  or or_7 (d_2, and_21_out, and_22_out, and_23_out, and_24_out);
endmodule

module main (
  input  [3:0] \input ,
  input  interruptor
);

  wire clock_1_out, FF_D_out_6, FF_D_out_7, FF_D_out_8, FF_D_out_9, L__Salida_a_2, L__Salida_b_2,
       L__Salida_c_2, L__Salida_d_2, L__Salida_e, L__Salida_f, L__Salida_g;
  wire [3:0] FF_D_out_13, multiplexer_1_out;

  Multiplexer #(.width(4)) multiplexer_1 (
    .in0(\input ), .in1(FF_D_out_13), .out(multiplexer_1_out), .sel(interruptor));  // open: en
  Clock clock_1 (.out(clock_1_out));
  FF_D FF_D (
    .in_1(clock_1_out), .in_2(multiplexer_1_out[3]), .in_3(multiplexer_1_out[2]),
    .in_4(multiplexer_1_out[1]), .in_5(multiplexer_1_out[0]), .out_6(FF_D_out_6), .out_7(FF_D_out_7),
    .out_8(FF_D_out_8), .out_9(FF_D_out_9), .out_10(FF_D_out_13[3]), .out_11(FF_D_out_13[2]),
    .out_12(FF_D_out_13[1]), .out_13(FF_D_out_13[0]));
  _7_sig L__Salida (
    .A(FF_D_out_6), .B(FF_D_out_7), .C(FF_D_out_8), .D(FF_D_out_9), .a_2(L__Salida_a_2), .b_2(L__Salida_b_2),
    .c_2(L__Salida_c_2), .d_2(L__Salida_d_2), .e(L__Salida_e), .f(L__Salida_f), .g(L__Salida_g));
  _7_Segment_Display u_7_segment_display_1 (
    .g(L__Salida_g), .f(L__Salida_f), .a(L__Salida_a_2), .b(L__Salida_b_2), .e(L__Salida_e),
    .d(L__Salida_d_2), .c(L__Salida_c_2));  // open: dp
endmodule
